# Fritzing sketch SynapsePod Crystal Circuit (saved by Fritzing 1.0.0rc)
circuit board: 8.28324cm x 9.78469cm
breadboards: 1

parts:
  Raspberry_PI_Pico_W = Raspberry Pi Pico W
  Keyboard = Generic 4x4 Keypad
  S2 = Pushbutton [package="[THT]"]
  LCD1 = Waveshare 2.4in LCD display

nets:
  N1: Raspberry_PI_Pico_W.pin_4, LCD1.pin_8
  N2: Raspberry_PI_Pico_W.pin_5, LCD1.pin_7
  N3: Raspberry_PI_Pico_W.pin_6, LCD1.pin_6
  N4: Raspberry_PI_Pico_W.pin_7, LCD1.pin_5
  N5: Raspberry_PI_Pico_W.pin_9, LCD1.pin4
  N6: Raspberry_PI_Pico_W.pin_10, LCD1.pin3
  N7: Raspberry_PI_Pico_W.pin_11, Raspberry_PI_Pico_W.pin_12, Raspberry_PI_Pico_W.pin_17, Keyboard.C4, Keyboard.C3, Keyboard.R2
  N8: Raspberry_PI_Pico_W.pin_13, Raspberry_PI_Pico_W.pin_18, Raspberry_PI_Pico_W.pin_28, Raspberry_PI_Pico_W.pin_38, Raspberry_PI_Pico_W.pin_42, S2.Pin_2, LCD1.pin2
  N9: Raspberry_PI_Pico_W.pin_14, Keyboard.C2
  N10: Raspberry_PI_Pico_W.pin_15, Keyboard.C1
  N11: Raspberry_PI_Pico_W.pin_16, Keyboard.R1
  N12: Raspberry_PI_Pico_W.pin_19, Keyboard.R3
  N13: Raspberry_PI_Pico_W.pin_20, Keyboard.R4
  N14: Raspberry_PI_Pico_W.pin_30, S2.Pin_4
  N15: Raspberry_PI_Pico_W.pin_36, LCD1.pin_1

custom parts:
  Raspberry Pi Pico W: Raspberry Pi Pico W. Based around the RP2040 microcontroller the Pico W is a low cost microcontroller device bringing Raspberry Pi quality, cost, and easy of use to the microcontroller space. The areas marked KEEPOUT in pcb silkscreen should not have traces running through them to avoid shorts on a soldered in module!
  Generic 4x4 Keypad: generic 4x4 keypad 4 rows of four 6 mm tact switches cheap and nasty but works
  Waveshare 2.4in LCD display: This is a generic 1.8 tft spi lcd display available on ebay and others. 240×320, General 2.4inch LCD Display Module, 65K RGB.
